# Fritzing sketch seizure_detector_schematic (saved by Fritzing 0.7.11b)
breadboards: 1

parts:
  Nano1 = Arduino Nano v2.3
  Part1 = Real Time Clock Module - DS1307 RTC Breakout Board  # not connected
  J1 = Piezo Speaker
  U1 = microSD Socket [package="Molex 502774-0891 [SMD]"]  # not connected
  Part2 = DeadOn RTC - DS3234 Breakout  # not connected
  Part3 = SD Card Module  # not connected

nets:
  N1: Nano1.GND, J1.pin2
  N2: Nano1.D4, J1.pin1

custom parts:
  SD Card Module: Description: SPI Bus SD Card Module
